# Fritzing sketch Running LED (saved by Fritzing 0.9.3b)
breadboards: 1

parts:
  Part1 = Arduino Uno (Rev3) - ICSP
  LED1 = LED - 5mm [color="Red (633nm)" package="5 mm [THT]"]
  LED2 = LED - 5mm [color="Red (633nm)" package="5 mm [THT]"]
  LED3 = LED - 5mm [color="Red (633nm)" package="5 mm [THT]"]
  R1 = 330 Ω Resistor [package=THT]
  R2 = 330 Ω Resistor [package=THT]
  R3 = 330 Ω Resistor [package=THT]

nets:
  N1: Part1.GND, LED1.cathode, LED2.cathode, LED3.cathode
  N2: Part1.D8, R3.Pin_0
  N3: Part1.D9_PWM, R2.Pin_0
  N4: Part1.D10_PWM/SS, R1.Pin_0
  N5: LED1.anode, R1.Pin_1
  N6: LED2.anode, R2.Pin_1
  N7: LED3.anode, R3.Pin_1

custom parts:
  330 Ω Resistor: A generic resistor (0.25W)
